// Logisim project s-mips.circ as structural Verilog: 16 circuits, main circuit S-MIPS Board
module S_MIPS_Board (
  input  DESHABILITAR_DISPATCHER,
  output halt
);

  wire button_1_out, CLK, CS, d_ff_1_q, LCLR, LoadRAM, LoadRAMOn, LW, R_R_W, R_W, ram_dispatcher_1_finished,
       RCS, Reset_out, RST, TTY_EN;
  wire [2:0] KDB;
  wire [3:0] LMask, Mask, ram_1_read_time, ram_1_write_time, RMask;
  wire [6:0] KDB_DATA, TTY_DATA;
  wire [15:0] Addr, LAddr, RAddr;
  wire [31:0] I0, I1, I2, I3, LData, ram_1_data_out_0, ram_1_data_out_1, ram_1_data_out_2, ram_1_data_out_3,
       RI0, RI1, RI2, RI3;

  TTY #(.rows(25), .cols(80)) tty_1 (.data(TTY_DATA), .clk(CLK), .we(TTY_EN), .clr(RST));
  not not_1 (LoadRAMOn, ram_dispatcher_1_finished);
  RAM_Dispatcher ram_dispatcher_1 (
    .WriteTime(ram_1_write_time), .Clock(CLK), .Data(LData), .Address(LAddr), .Mask(LMask),
    .Finished(ram_dispatcher_1_finished), .Write(LW), .CLR(LCLR));
  Keyboard #(.buflen(64)) keyboard_1 (.clk(CLK), .re(KDB[0]), .avail(KDB[2]), .data(KDB_DATA));  // open: clr
  RAM ram_1 (
    .Address(RAddr), .Data_Out_0(ram_1_data_out_0), .Data_Out_1(ram_1_data_out_1),
    .Data_Out_2(ram_1_data_out_2), .Data_Out_3(ram_1_data_out_3), .Data_In_0(RI0), .Data_In_1(RI1),
    .Data_In_2(RI2), .Data_In_3(RI3), .Mask(RMask), .nRead_Write(R_R_W), .Chip_Select(RCS),
    .Read_Time(ram_1_read_time), .Reset(button_1_out), .Write_Time(ram_1_write_time));
  Button button_1 (.out(button_1_out));
  D_Flip_Flop d_ff_1 (.clk(CLK), .D(1'b1), .Q(d_ff_1_q), .reset(Reset_out));  // open: Qn, preset, en
  Button Reset (.out(Reset_out));
  S_MIPS s_mips_1 (
    .Kbd_Enable(KDB[0]), .Address(Addr), .Kbd_Clear(KDB[1]), .Kbd_Available(KDB[2]), .RAM_In_0(I0),
    .Kbd_ASCII_Data(KDB_DATA), .RAM_In_1(I1), .TTY_Enable(TTY_EN), .RAM_In_2(I2), .RAM_In_3(I3), .Reset(RST),
    .RAM_Out_0(ram_1_data_out_0), .Clock(CLK), .RAM_Out_1(ram_1_data_out_1), .Stop(halt),
    .RAM_Out_2(ram_1_data_out_2), .RAM_Out_3(ram_1_data_out_3), .Mask(Mask), .Read_Time(ram_1_read_time),
    .Write_Time(ram_1_write_time), .nRead_Write(R_W), .Chip_Select(CS), .TTY_ASCII_Data(TTY_DATA));
  D_Flip_Flop d_ff_2 (.clk(CLK), .D(d_ff_1_q), .Qn(LCLR), .reset(Reset_out));  // open: Q, preset, en
  or or_1 (RST, LCLR, LoadRAM);
  Clock clock_1 (.out(CLK));
  Multiplexer #(.width(32), .enable("false")) multiplexer_1 (.in0(I0), .in1(LData), .out(RI0), .sel(LoadRAM));
  Multiplexer #(.width(32), .enable("false")) multiplexer_2 (.in0(I1), .in1(LData), .out(RI1), .sel(LoadRAM));
  Multiplexer #(.width(32), .enable("false")) multiplexer_3 (.in0(I2), .in1(LData), .out(RI2), .sel(LoadRAM));
  Multiplexer #(.width(32), .enable("false")) multiplexer_4 (.in0(I3), .in1(LData), .out(RI3), .sel(LoadRAM));
  and and_1 (LoadRAM, ~DESHABILITAR_DISPATCHER, LoadRAMOn);  // AND_Gate
  Multiplexer #(.width(16), .enable("false")) multiplexer_5 (.in0(Addr), .in1(LAddr), .out(RAddr), .sel(LoadRAM));
  Multiplexer #(.width(4), .enable("false")) multiplexer_6 (.in0(Mask), .in1(LMask), .out(RMask), .sel(LoadRAM));
  Multiplexer #(.enable("false")) multiplexer_7 (.in0(CS), .in1(LW), .out(RCS), .sel(LoadRAM));
  Multiplexer #(.enable("false")) multiplexer_8 (.in0(R_W), .in1(LW), .out(R_R_W), .sel(LoadRAM));

  // Notes on the sheet:
  //   NO MODIFICAR
  //   Keyboard
endmodule

module RAM (
  input  [15:0] Address,
  input  [31:0] Data_In_0,
  input  [31:0] Data_In_1,
  input  [31:0] Data_In_2,
  input  [31:0] Data_In_3,
  input  [3:0] Mask,
  input  nRead_Write,
  input  Chip_Select,
  input  Reset,
  output [31:0] Data_Out_0,
  output [31:0] Data_Out_1,
  output [31:0] Data_Out_2,
  output [31:0] Data_Out_3,
  output [3:0] Read_Time,
  output [3:0] Write_Time
);

  wire and_2_out, and_3_out, and_4_out, and_5_out, and_6_out, and_7_out, and_8_out, and_9_out, Changed, CLK,
       comparator_2_eq, comparator_3_eq, comparator_4_eq, comparator_5_eq, comparator_6_eq, Count,
       demultiplexer_3_out0, Idle, Idle_q, Load, Load0, Load1, nand_1_out, or_1_out, or_2_out, or_3_out,
       or_4_out, or_5_out, or_6_out, or_7_out, or_8_out, or_9_out, or_10_out, Proc_q, Update_Mem, Zero_Time;
  wire [3:0] counter_1_q, multiplexer_1_out, subtractor_1_out;
  wire [31:0] register_1_q, register_2_q, register_3_q, register_4_q, register_5_q;

  // Probe on 4'b0011
  // Probe on 4'b0010
  Multiplexer #(.width(4), .enable("false")) multiplexer_1 (
    .in0(4'b0011), .in1(4'b0010), .out(multiplexer_1_out), .sel(nRead_Write));
  or or_1 (or_1_out, Idle, Update_Mem);
  or or_2 (or_2_out, ~Chip_Select, Reset);  // OR_Gate
  Subtractor #(.width(4)) subtractor_1 (.a(multiplexer_1_out), .b(4'b0010), .out(subtractor_1_out));  // open: bin, bout
  D_Flip_Flop u_Idle (.clk(CLK), .D(or_1_out), .Q(Idle_q), .preset(or_2_out));  // open: Qn, en, reset
  Demultiplexer #(.enable("false")) demultiplexer_1 (.out0(Idle), .out1(Load0), .in(Idle_q), .sel(Changed));
  // Probe on counter_1_q
  Counter #(.width(4), .max('hf)) counter_1 (
    .load(Load), .D(subtractor_1_out), .count(Count), .Q(counter_1_q), .clk(CLK), .clr(or_3_out));  // open: carry
  or or_3 (or_3_out, ~Chip_Select, Reset);  // OR_Gate
  Comparator #(.width(4), .mode("unsigned")) comparator_1 (
    .a(4'b0000), .b(counter_1_q), .eq(Zero_Time));  // open: gt, lt
  or or_4 (or_4_out, Count, Load0, Load1);
  Register #(.width(32)) register_1 (.D(Data_In_0), .en(Chip_Select), .Q(register_1_q), .clk(CLK), .clr(or_5_out));
  or or_5 (or_5_out, ~Chip_Select, Reset);  // OR_Gate
  Register #(.width(32)) register_2 (.D(Data_In_1), .en(Chip_Select), .Q(register_2_q), .clk(CLK), .clr(or_6_out));
  or or_6 (or_6_out, ~Chip_Select, Reset);  // OR_Gate
  Register #(.width(32)) register_3 (.D(Data_In_2), .en(Chip_Select), .Q(register_3_q), .clk(CLK), .clr(or_7_out));
  or or_7 (or_7_out, ~Chip_Select, Reset);  // OR_Gate
  Register #(.width(32)) register_4 (.D(Data_In_3), .en(Chip_Select), .Q(register_4_q), .clk(CLK), .clr(or_8_out));
  or or_8 (or_8_out, ~Chip_Select, Reset);  // OR_Gate
  Register #(.width(32)) register_5 (
    .D({{11{1'b1}}, nRead_Write, Mask, Address}), .en(Chip_Select), .Q(register_5_q), .clk(CLK),
    .clr(or_9_out));
  or or_9 (or_9_out, ~Chip_Select, Reset);  // OR_Gate
  D_Flip_Flop Proc (.clk(CLK), .D(or_4_out), .Q(Proc_q), .reset(or_10_out));  // open: Qn, preset, en
  or or_10 (or_10_out, ~Chip_Select, Reset);  // OR_Gate
  Demultiplexer #(.enable("false")) demultiplexer_2 (
    .out0(Count), .out1(Update_Mem), .in(demultiplexer_3_out0), .sel(Zero_Time));
  Demultiplexer #(.enable("false")) demultiplexer_3 (
    .out0(demultiplexer_3_out0), .out1(Load1), .in(Proc_q), .sel(Changed));
  Clock clock_1 (.out(CLK));
  Comparator #(.width(32)) comparator_2 (.a(register_1_q), .b(Data_In_0), .eq(comparator_2_eq));  // open: gt, lt
  Comparator #(.width(32)) comparator_3 (.a(register_2_q), .b(Data_In_1), .eq(comparator_3_eq));  // open: gt, lt
  Comparator #(.width(32)) comparator_4 (.a(register_3_q), .b(Data_In_2), .eq(comparator_4_eq));  // open: gt, lt
  Comparator #(.width(32)) comparator_5 (.a(register_4_q), .b(Data_In_3), .eq(comparator_5_eq));  // open: gt, lt
  Comparator #(.width(32)) comparator_6 (
    .a(register_5_q), .b({{11{1'b1}}, nRead_Write, Mask, Address}), .eq(comparator_6_eq));  // open: gt, lt
  nand nand_1 (nand_1_out, comparator_6_eq, comparator_2_eq, comparator_3_eq, comparator_4_eq, comparator_5_eq);
  and and_1 (Changed, nand_1_out, Chip_Select);
  or or_11 (Load, Count, Load1, Load0);
  and and_2 (and_2_out, Mask[0], Update_Mem, nRead_Write);
  and and_3 (and_3_out, Mask[1], Update_Mem, nRead_Write);
  and and_4 (and_4_out, Mask[2], Update_Mem, nRead_Write);
  and and_5 (and_5_out, Mask[3], Update_Mem, nRead_Write);
  RAM_part #(.addrWidth(16), .dataWidth(32), .bus("separate")) ram_1 (
    .addr(Address), .din(Data_In_0), .data(Data_Out_0), .str(and_2_out), .sel(Chip_Select), .clk(CLK),
    .ld(and_6_out), .clr(Reset));
  and and_6 (and_6_out, ~nRead_Write, Idle);  // AND_Gate
  RAM_part #(.addrWidth(16), .dataWidth(32), .bus("separate")) ram_2 (
    .addr(Address), .din(Data_In_1), .data(Data_Out_1), .str(and_3_out), .sel(Chip_Select), .clk(CLK),
    .ld(and_7_out), .clr(Reset));
  and and_7 (and_7_out, ~nRead_Write, Idle);  // AND_Gate
  RAM_part #(.addrWidth(16), .dataWidth(32), .bus("separate")) ram_3 (
    .addr(Address), .din(Data_In_2), .data(Data_Out_2), .str(and_4_out), .sel(Chip_Select), .clk(CLK),
    .ld(and_8_out), .clr(Reset));
  and and_8 (and_8_out, ~nRead_Write, Idle);  // AND_Gate
  RAM_part #(.addrWidth(16), .dataWidth(32), .bus("separate")) ram_4 (
    .addr(Address), .din(Data_In_3), .data(Data_Out_3), .str(and_5_out), .sel(Chip_Select), .clk(CLK),
    .ld(and_9_out), .clr(Reset));
  and and_9 (and_9_out, ~nRead_Write, Idle);  // AND_Gate

  assign Read_Time = 4'b0011;
  assign Write_Time = 4'b0010;

  // Other names for the same wires on the sheet: M0 = Mask[0]; M1 = Mask[1]; M2 = Mask[2]; M3 = Mask[3];
  //   RW = nRead_Write; CLR = Reset; CS = Chip_Select; Load2 = Count

  // Notes on the sheet:
  //   NO MODIFICAR
  //   excepto quizás los valores RT y WT
  //   BANK0
  //   BANK1
  //   BANK2
  //   BANK3
endmodule

module S_MIPS (
  input  Kbd_Available,
  input  [6:0] Kbd_ASCII_Data,
  input  [31:0] RAM_Out_0,
  input  [31:0] RAM_Out_1,
  input  [31:0] RAM_Out_2,
  input  Reset,
  input  Clock,
  input  [31:0] RAM_Out_3,
  input  [3:0] Read_Time,
  input  [3:0] Write_Time,
  output Kbd_Enable,
  output [15:0] Address,
  output Kbd_Clear,
  output TTY_Enable,
  output [6:0] TTY_ASCII_Data,
  output Stop,
  output [31:0] RAM_In_0,
  output [31:0] RAM_In_1,
  output [31:0] RAM_In_2,
  output [31:0] RAM_In_3,
  output [3:0] Mask,
  output nRead_Write,
  output Chip_Select
);

  wire ADD, ADDi, AND, ANDi, BEQ, BGTZ, BLEZ, BLTZ, BNEQ, CLEAR, CLR_M, CLRI, demultiplexer_1_out1,
       demultiplexer_3_out0, demultiplexer_3_out1, demultiplexer_4_out0, DIV, DIVU, EF, EI, EL, HALT, IDLE_q,
       J, JR, KBD, LI, Lo_Hi_W, LPC, LW, M_C, MC_End, MFHi, MFLo, MULT, MULU, NF, NOP, NOR, nR_W, OR,
       or_2_out, or_4_out, or_5_out, or_7_out, ORi, POP, Pop_Load, PUSH, Push_Load, Push_Pop, R_W, RI_q, RND,
       RT_S, SLT, SLTi, SLTiU, SLTU, Stack_Inst, Start_MC, Start_MC0, Start_MC1, SUB, SW, TTY, XOR, XORi, ZF;
  wire [1:0] ALU_RB_S;
  wire [2:0] RF_DATA_IN_S;
  wire [3:0] FS;
  wire [4:0] multiplexer_5_out, RD, RS, RT;
  wire [15:0] K_Offset;
  wire [25:0] Etiqueta_Destino;
  wire [31:0] bcu_1_new_pc, Hi, Instruction, Instruction_q, K_Xi_L, K_Xi_No_L, Low, multiplexer_1_out,
       multiplexer_2_out, multiplexer_3_out, multiplexer_4_out, multiplexer_6_out, OALU, Out_HI, Out_Low, PC,
       RB, RND_OUT, SP;
  wire [31:7] RA;

  and and_1 (TTY_Enable, TTY, EI);
  Register #(.width(32)) u_Instruction (.D(Instruction), .en(LI), .Q(Instruction_q), .clk(Clock), .clr(CLRI));
  BCU bcu_1 (
    .BEQ(BEQ), .NF(NF), .ZF(ZF), .BNE(BNEQ), .EF(EF), .BLEZ(BLEZ), .PC(PC), .BLTZ(BLTZ), .BGTZ(BGTZ),
    .REGISTER({RA, TTY_ASCII_Data}), .J(J), .JR(JR), .Etiqueta_Destino(Etiqueta_Destino), .Offset(K_Offset),
    .New_PC(bcu_1_new_pc));
  Demultiplexer #(.enable("false")) demultiplexer_1 (
    .out1(demultiplexer_1_out1), .in(IDLE_q), .sel(Reset));  // open: out0
  D_Flip_Flop IDLE (.clk(Clock), .Q(IDLE_q), .preset(Reset));  // open: D, Qn, en, reset
  or or_1 (CLRI, CLEAR, Reset);
  Register #(.width(32)) u_PC (.D(bcu_1_new_pc), .en(LPC), .Q(PC), .clk(Clock), .clr(Reset));
  INSTRUCTION_DECODER instruction_decoder_1 (
    .Data_In(Instruction_q), .Nop(NOP), .TTY(TTY), .MFLO(MFLo), .SLT(SLT), .MULU(MULU), .AND(AND), .XOR(XOR),
    .BLEZ(BLEZ), .J(J), .PUSH(PUSH), .ADDi(ADDi), .ORi(ORi), .Halt(HALT), .KBD(KBD), .ADD(ADD), .SLTU(SLTU),
    .DIV(DIV), .OR(OR), .BEQ(BEQ), .BGTZ(BGTZ), .JR(JR), .LW(LW), .SLTi(SLTi), .XORi(XORi), .RND(RND),
    .MFHI(MFHi), .SUB(SUB), .MULT(MULT), .DIVU(DIVU), .NOR(NOR), .BNEQ(BNEQ), .BLTZ(BLTZ), .POP(POP),
    .SW(SW), .ANDi(ANDi), .SLTiU(SLTiU), .Registro_Destino(RD), .Constante(K_Offset), .RT(RT),
    .\Constante_Inmed_No_Lógica (K_Xi_No_L), .Destino__Jump(Etiqueta_Destino), .RS(RS),
    .\Constante_Inmed_Lógica (K_Xi_L));
  or or_2 (or_2_out, Start_MC1, demultiplexer_4_out0, demultiplexer_1_out1, CLEAR);
  Multiplexer #(.width(32), .enable("false")) multiplexer_1 (
    .in0(PC), .in1(SP), .out(multiplexer_1_out), .sel(Stack_Inst));
  Multiplexer #(.select(2), .width(32), .enable("false")) multiplexer_2 (
    .in0(RB), .in1(K_Xi_L), .in2(K_Xi_No_L), .out(multiplexer_2_out), .sel(ALU_RB_S));  // open: in3
  D_Flip_Flop RI (.clk(Clock), .D(or_2_out), .Q(RI_q));  // open: Qn, preset, en, reset
  Demultiplexer #(.enable("false")) demultiplexer_2 (.out0(Start_MC1), .out1(LI), .in(RI_q), .sel(MC_End));
  or or_3 (CLR_M, LI, Reset, CLEAR);
  Random #(.width(32)) random_1 (.clk(Clock), .next(RND), .out(RND_OUT));  // open: clr
  Multiplexer #(.width(32), .enable("false")) multiplexer_3 (
    .in0(multiplexer_1_out), .in1(OALU), .out(multiplexer_3_out), .sel(or_4_out));
  or or_4 (or_4_out, LW, SW);
  MC mc_1 (
    .Start(Start_MC), .RAM_Out_0(RAM_Out_0), .Clock(Clock), .Reset(CLR_M), .RAM_Out_1(RAM_Out_1),
    .Read_Time(Read_Time), .Write_Time(Write_Time), .RAM_Out_2(RAM_Out_2), .R_W_Selector(nR_W),
    .Finish(MC_End), .RAM_Out_3(RAM_Out_3), .Mask(Mask), .nRead_Write(nRead_Write), .Out(Instruction),
    .Chip_Select(Chip_Select), .Address(Address), .RAM_In_0(RAM_In_0), .RAM_In_1(RAM_In_1),
    .RAM_In_2(RAM_In_2), .RAM_In_3(RAM_In_3), .Offset(multiplexer_3_out), .Registro(multiplexer_4_out));
  Multiplexer #(.width(32), .enable("false")) multiplexer_4 (
    .in0(RB), .in1({RA, TTY_ASCII_Data}), .out(multiplexer_4_out), .sel(Stack_Inst));
  ALU alu_1 (
    .SL(FS), .OutputALU(OALU), .B(multiplexer_2_out), .out_7(Out_Low), .Equality_Flag(EF), .Zero_Flag(NF),
    .Negative_Flag(ZF), .Clock(Clock), .Reset(Reset), .OUT_Hi(Out_HI), .in_1({RA, TTY_ASCII_Data}));
  Multiplexer #(.width(5), .enable("false")) multiplexer_5 (.in0(RD), .in1(RT), .out(multiplexer_5_out), .sel(RT_S));
  or or_5 (or_5_out, Stop, demultiplexer_3_out1);
  D_Flip_Flop u_EI (.clk(Clock), .D(LI), .Q(EI), .reset(Reset));  // open: Qn, preset, en
  Demultiplexer #(.enable("false")) demultiplexer_3 (
    .out0(demultiplexer_3_out0), .out1(demultiplexer_3_out1), .in(EI), .sel(HALT));
  D_Flip_Flop END (.clk(Clock), .D(or_5_out), .Q(Stop), .reset(Reset));  // open: Qn, preset, en
  or or_6 (Start_MC, Start_MC0, Start_MC1);
  Demultiplexer #(.enable("false")) demultiplexer_4 (
    .out0(demultiplexer_4_out0), .out1(Push_Load), .in(demultiplexer_3_out0), .sel(M_C));
  Multiplexer #(.select(3), .width(32), .enable("false")) multiplexer_6 (
    .in0(OALU), .in1(RND_OUT), .in2(Instruction), .in3(Instruction), .in4(Hi), .in5(Low),
    .in6({{25{1'b0}}, Kbd_ASCII_Data}), .in7({32{1'b1}}), .out(multiplexer_6_out), .sel(RF_DATA_IN_S));
  RF rf_1 (
    .Clock(Clock), .RW(R_W), .Out_A({RA, TTY_ASCII_Data}), .Out_B(RB), .RS(multiplexer_5_out), .CRL(Reset),
    .AS(RS), .BS(RT), .HI(Out_HI), .Low(Out_Low), .HI_Low(Lo_Hi_W), .Push_pop(Push_Pop),
    .Stack_Instruction(Stack_Inst), .DATA(multiplexer_6_out), .Push_Load(Push_Load), .Pop_Load(Pop_Load),
    .HI_Output(Hi), .Low_Output(Low), .SP_Output(SP));
  or or_7 (or_7_out, Start_MC0, Push_Load);
  D_Flip_Flop WFM (.clk(Clock), .D(or_7_out), .Q(EL), .reset(Reset));  // open: Qn, preset, en
  Demultiplexer #(.enable("false")) demultiplexer_5 (.out0(Start_MC0), .out1(Pop_Load), .in(EL), .sel(MC_End));
  D_Flip_Flop EMI (.clk(Clock), .D(Pop_Load), .Q(CLEAR));  // open: Qn, preset, en, reset
  CU cu_1 (
    .Function_Selector(FS), .Stack_Inst(Stack_Inst), .Push_Pop(Push_Pop), .R_W(R_W), .Lo_Hi_Write(Lo_Hi_W),
    .Halt(HALT), .DIVU(DIVU), .ALU_S(ALU_RB_S), .Nop(NOP), .BEQ(BEQ), .RF_S(RF_DATA_IN_S), .TTY(TTY),
    .BNEQ(BNEQ), .RT_S(RT_S), .RND(RND), .BLEZ(BLEZ), .R_W_M(M_C), .KBD(KBD), .BGTZ(BGTZ), .L_PC(LPC),
    .MFHI(MFHi), .BLTZ(BLTZ), .nR_W(nR_W), .MFLO(MFLo), .J(J), .KBD_AV(Kbd_Available), .ADD(ADD), .JR(JR),
    .KBD_EN(Kbd_Enable), .SUB(SUB), .POP(POP), .SLT(SLT), .PUSH(PUSH), .SLTU(SLTU), .ADDi(ADDi), .AND(AND),
    .SLTi(SLTi), .OR(OR), .SLTUi(SLTiU), .NOR(NOR), .ANDi(ANDi), .XOR(XOR), .ORi(ORi), .MULT(MULT),
    .XORi(XORi), .DIV(DIV), .LW(LW), .MULU(MULU), .SW(SW), .EI(EI), .EM(EL));

  assign Kbd_Clear = Reset;

  // Other names for the same wires on the sheet: KBD_DATA[6:0] = Kbd_ASCII_Data; CLK = Clock; CLR = Reset;
  //   CRI = CLEAR; CS = Chip_Select; KBD_AVAIL = Kbd_Available; Memoria[31:0] = Instruction; Pila[31:0] = Instruction;
  //   RA[6:0] = TTY_ASCII_Data; RAM_A[15:0] = Address; RAM_INPUT_0[31:0] = RAM_In_0; RAM_INPUT_1[31:0] = RAM_In_1;
  //   RAM_INPUT_2[31:0] = RAM_In_2; RAM_INPUT_3[31:0] = RAM_In_3; RAM_MASK[3:0] = Mask;
  //   RAM_OUTPUT_0[31:0] = RAM_Out_0; RAM_OUTPUT_1[31:0] = RAM_Out_1; RAM_OUTPUT_2[31:0] = RAM_Out_2;
  //   RAM_OUTPUT_3[31:0] = RAM_Out_3; RW = nRead_Write

  // Notes on the sheet:
  //   RAM ADDRESS
  //   DATA FROM RAM
  //   DATA TO RAM
  //   DATA WRITE MASK
  //   RAM TIMING
  //   RAM CONTROL
  //   KEYBOARD
  //   TTY
  //   SEQUENCING
endmodule

module RAM_Dispatcher (
  input  [3:0] WriteTime,
  input  Clock,
  input  CLR,
  output [31:0] Data,
  output [15:0] Address,
  output [3:0] Mask,
  output Finished,
  output Write
);

  wire demultiplexer_2_out1, demultiplexer_3_out1, End, IDLE_q, IncAddr, Load, or_1_out, or_2_out, While_q,
       WriteEnd;
  wire [3:0] counter_1_q;
  wire [31:0] CurrentAddress_q;

  Counter #(.width(32), .max('hffffffff)) CurrentAddress (
    .count(IncAddr), .Q({CurrentAddress_q[31:18], Address, CurrentAddress_q[1:0]}), .clk(Clock), .clr(CLR));  // open: load, D, carry
  or or_1 (or_1_out, IncAddr, demultiplexer_3_out1, Finished);
  D_Flip_Flop IDLE (.clk(Clock), .D(or_1_out), .Q(IDLE_q), .preset(CLR));  // open: Qn, en, reset
  Demultiplexer #(.enable("false")) demultiplexer_1 (.out0(Load), .out1(Finished), .in(IDLE_q), .sel(End));
  D_Flip_Flop While (.clk(Clock), .D(or_2_out), .Q(While_q), .reset(CLR));  // open: Qn, preset, en
  or or_2 (or_2_out, Write, Load);
  RAM_part #(.addrWidth(18), .dataWidth(32)) ram_1 (
    .addr({Address, CurrentAddress_q[1:0]}), .data(Data), .clk(Clock));  // open: sel, ld, clr
  Demultiplexer #(.enable("false")) demultiplexer_2 (
    .out0(Write), .out1(demultiplexer_2_out1), .in(While_q), .sel(WriteEnd));
  Decoder #(.select(2)) decoder_1 (
    .out0(Mask[0]), .out1(Mask[1]), .out2(Mask[2]), .out3(Mask[3]), .sel(CurrentAddress_q[1:0]));  // open: en
  Demultiplexer #(.enable("false")) demultiplexer_3 (
    .out0(IncAddr), .out1(demultiplexer_3_out1), .in(demultiplexer_2_out1), .sel(End));
  Counter #(.width(4), .max('hf)) counter_1 (
    .load(Load), .D(WriteTime), .count(Write), .Q(counter_1_q), .clk(Clock));  // open: carry, clr
  Comparator #(.width(32)) comparator_1 (.a(Data), .b({32{1'b1}}), .eq(End));  // open: gt, lt
  Comparator #(.width(4)) comparator_2 (.a(4'b0000), .b(counter_1_q), .eq(WriteEnd));  // open: gt, lt

  // Other names for the same wires on the sheet: CLK = Clock; Count = Write; WT[3:0] = WriteTime
endmodule

module RF (
  input  Push_pop,
  input  Stack_Instruction,
  input  Clock,
  input  CRL,
  input  RW,
  input  HI_Low,
  input  [4:0] RS,
  input  [4:0] AS,
  input  [4:0] BS,
  input  [31:0] DATA,
  input  [31:0] HI,
  input  [31:0] Low,
  input  Pop_Load,
  input  Push_Load,
  output [31:0] Out_A,
  output [31:0] Out_B,
  output [31:0] SP_Output,
  output [31:0] HI_Output,
  output [31:0] Low_Output
);

  wire and_1_out, and_2_out, E1, E2, E3, E4, E5, E6, E7, E8, E9, E10, E11, E12, E13, E14, E15, E16, E17, E18,
       E19, E20, E21, E22, E23, E24, E25, E26, E27, E28, E29, E30, E31, E31_1;
  wire [31:0] _1, _2, _3, _4, _5, _6, _7, _8, _9, _10, _11, _12, _13, _14, _15, _16, _17, _18, _19, _20, _21,
       _22, _23, _24, _25, _26, _27, _28, _29, _30, adder_1_out, In31, multiplexer_1_out;

  Register #(.width(32)) R1 (.D(DATA), .en(E1), .Q(_1), .clk(Clock), .clr(CRL));
  Register #(.width(32)) R2 (.D(DATA), .en(E2), .Q(_2), .clk(Clock), .clr(CRL));
  Register #(.width(32)) R3 (.D(DATA), .en(E3), .Q(_3), .clk(Clock), .clr(CRL));
  Register #(.width(32)) R4 (.D(DATA), .en(E4), .Q(_4), .clk(Clock), .clr(CRL));
  Register #(.width(32)) R5 (.D(DATA), .en(E5), .Q(_5), .clk(Clock), .clr(CRL));
  Register #(.width(32)) R6 (.D(DATA), .en(E6), .Q(_6), .clk(Clock), .clr(CRL));
  Register #(.width(32)) R7 (.D(DATA), .en(E7), .Q(_7), .clk(Clock), .clr(CRL));
  Register #(.width(32)) R8 (.D(DATA), .en(E8), .Q(_8), .clk(Clock), .clr(CRL));
  Register #(.width(32)) u_HI (.D(HI), .en(HI_Low), .Q(HI_Output), .clk(Clock), .clr(CRL));
  Register #(.width(32)) R9 (.D(DATA), .en(E9), .Q(_9), .clk(Clock), .clr(CRL));
  Register #(.width(32)) R10 (.D(DATA), .en(E10), .Q(_10), .clk(Clock), .clr(CRL));
  Register #(.width(32)) R11 (.D(DATA), .en(E11), .Q(_11), .clk(Clock), .clr(CRL));
  Register #(.width(32)) R12 (.D(DATA), .en(E12), .Q(_12), .clk(Clock), .clr(CRL));
  Register #(.width(32)) R13 (.D(DATA), .en(E13), .Q(_13), .clk(Clock), .clr(CRL));
  Register #(.width(32)) R14 (.D(DATA), .en(E14), .Q(_14), .clk(Clock), .clr(CRL));
  Register #(.width(32)) R15 (.D(DATA), .en(E15), .Q(_15), .clk(Clock), .clr(CRL));
  Register #(.width(32)) R16 (.D(DATA), .en(E16), .Q(_16), .clk(Clock), .clr(CRL));
  Register #(.width(32)) register_1 (.D(Low), .en(HI_Low), .Q(Low_Output), .clk(Clock), .clr(CRL));
  Register #(.width(32)) R17 (.D(DATA), .en(E17), .Q(_17), .clk(Clock), .clr(CRL));
  Register #(.width(32)) R18 (.D(DATA), .en(E18), .Q(_18), .clk(Clock), .clr(CRL));
  Register #(.width(32)) R19 (.D(DATA), .en(E11), .Q(_19), .clk(Clock), .clr(CRL));
  Register #(.width(32)) R20 (.D(DATA), .en(E12), .Q(_20), .clk(Clock), .clr(CRL));
  Register #(.width(32)) R21 (.D(DATA), .en(E21), .Q(_21), .clk(Clock), .clr(CRL));
  Register #(.width(32)) R22 (.D(DATA), .en(E22), .Q(_22), .clk(Clock), .clr(CRL));
  Register #(.width(32)) R23 (.D(DATA), .en(E23), .clk(Clock), .clr(CRL));  // open: Q
  Register #(.width(32)) R24 (.D(DATA), .en(E24), .Q(_24), .clk(Clock), .clr(CRL));
  Multiplexer #(.width(32), .enable("false")) multiplexer_1 (
    .in0(32'h4), .in1(32'hfffffffc), .out(multiplexer_1_out), .sel(Push_pop));
  Adder #(.width(32)) adder_1 (.a(SP_Output), .b(multiplexer_1_out), .out(adder_1_out));  // open: cin, cout
  Register #(.width(32)) R25 (.D(DATA), .en(E25), .Q(_25), .clk(Clock), .clr(CRL));
  Register #(.width(32)) R26 (.D(DATA), .en(E26), .Q(_26), .clk(Clock), .clr(CRL));
  Register #(.width(32)) R27 (.D(DATA), .en(E27), .Q(_27), .clk(Clock), .clr(CRL));
  Register #(.width(32)) R28 (.D(DATA), .en(E28), .Q(_28), .clk(Clock), .clr(CRL));
  Register #(.width(32)) R29 (.D(DATA), .en(E29), .Q(_29), .clk(Clock), .clr(CRL));
  Register #(.width(32)) R30 (.D(DATA), .en(E30), .Q(_30), .clk(Clock), .clr(CRL));
  Register #(.width(32)) R31 (.D(In31), .en(E31_1), .Q(SP_Output), .clk(Clock), .clr(CRL));
  Multiplexer #(.width(32), .enable("false")) multiplexer_2 (
    .in0(DATA), .in1(adder_1_out), .out(In31), .sel(Stack_Instruction));
  or or_1 (E31_1, and_1_out, E31, and_2_out);
  and and_1 (and_1_out, Push_Load, Push_pop);
  and and_2 (and_2_out, ~Push_pop, Pop_Load, Stack_Instruction);  // AND_Gate
  Demultiplexer #(.select(5), .enable("false")) demultiplexer_1 (
    .out1(E1), .out2(E2), .out3(E3), .out4(E4), .out5(E5), .out6(E6), .out7(E7), .out8(E8), .out9(E9),
    .out10(E10), .out11(E11), .out12(E12), .out13(E13), .out14(E14), .out15(E15), .out16(E16), .out17(E17),
    .out18(E18), .out19(E19), .out20(E20), .out21(E21), .out22(E22), .out23(E23), .out24(E24), .out25(E25),
    .out26(E26), .out27(E27), .out28(E28), .out29(E29), .out30(E30), .out31(E31), .in(RW), .sel(RS));  // open: out0
  Multiplexer #(.select(5), .width(32), .enable("false")) multiplexer_3 (
    .in0({32{1'b0}}), .in1(_1), .in2(_2), .in3(_3), .in4(_4), .in5(_5), .in6(_6), .in7(_7), .in8(_8),
    .in9(_9), .in10(_10), .in11(_11), .in12(_12), .in13(_13), .in14(_14), .in15(_15), .in16(_16), .in17(_17),
    .in18(_18), .in19(_19), .in20(_20), .in21(_21), .in22(_22), .in23(_23), .in24(_24), .in25(_25),
    .in26(_26), .in27(_27), .in28(_28), .in29(_29), .in30(_30), .in31(SP_Output), .out(Out_A), .sel(AS));
  Multiplexer #(.select(5), .width(32), .enable("false")) multiplexer_4 (
    .in0({32{1'b0}}), .in1(_1), .in2(_2), .in3(_3), .in4(_4), .in5(_5), .in6(_6), .in7(_7), .in8(_8),
    .in9(_9), .in10(_10), .in11(_11), .in12(_12), .in13(_13), .in14(_14), .in15(_15), .in16(_16), .in17(_17),
    .in18(_18), .in19(_19), .in20(_20), .in21(_21), .in22(_22), .in23(_23), .in24(_24), .in25(_25),
    .in26(_26), .in27(_27), .in28(_28), .in29(_29), .in30(_30), .in31(SP_Output), .out(Out_B), .sel(BS));

  // Other names for the same wires on the sheet: _31[31:0] = SP_Output; A[31:0] = Out_A; B[31:0] = Out_B; CLK = Clock;
  //   Reset = CRL; Si = Stack_Instruction

  // Notes on the sheet:
  //   Read or Write Bit (1 to write)
endmodule

module ALU (
  input  [31:0] in_1,
  input  [31:0] B,
  input  [3:0] SL,
  input  Clock,
  input  Reset,
  output [31:0] OUT_Hi,
  output [31:0] out_7,
  output Equality_Flag,
  output Zero_Flag,
  output Negative_Flag,
  output [31:0] OutputALU
);

  wire [31:0] adder_1_out, and_1_out, divider_1_out, divider_1_rem, divu_1_hi, divu_1_low, multiplier_1_cout,
       multiplier_1_out, mulu_1_hi, mulu_1_low, nor_1_out, or_1_out, slt_1_output, sltu_1_output,
       subtractor_1_out, xor_1_out;

  Adder #(.width(32)) adder_1 (.a(in_1), .b(B), .out(adder_1_out));  // open: cin, cout
  Subtractor #(.width(32)) subtractor_1 (.a(in_1), .b(B), .out(subtractor_1_out));  // open: bin, bout
  SLT slt_1 (.RS(in_1), .RT(B), .Output(slt_1_output));
  SLTU sltu_1 (.RS(in_1), .RT(B), .Output(sltu_1_output));
  assign and_1_out = in_1 & B;  // AND_Gate and_1, 32 bits wide
  assign or_1_out = in_1 | B;  // OR_Gate or_1, 32 bits wide
  assign nor_1_out = ~(in_1 | B);  // NOR_Gate nor_1, 32 bits wide
  assign xor_1_out = in_1 ^ B;  // XOR_Gate xor_1, 32 bits wide
  Comparator #(.width(32)) comparator_1 (.a(in_1), .b(B), .eq(Equality_Flag));  // open: gt, lt
  Comparator #(.width(32)) comparator_2 (.a(in_1), .b({32{1'b0}}), .eq(Zero_Flag), .lt(Negative_Flag));  // open: gt
  Multiplexer #(.select(3), .width(32), .enable("false")) multiplexer_1 (
    .in0(adder_1_out), .in1(subtractor_1_out), .in2(slt_1_output), .in3(sltu_1_output), .in4(and_1_out),
    .in5(or_1_out), .in6(nor_1_out), .in7(xor_1_out), .out(OutputALU), .sel(SL[2:0]));
  Multiplier #(.width(32)) multiplier_1 (
    .a(in_1), .b(B), .out(multiplier_1_out), .cout(multiplier_1_cout));  // open: cin
  DIVU divu_1 (.A(in_1), .B(B), .Low(divu_1_low), .Hi(divu_1_hi));
  MULU mulu_1 (.A(in_1), .B(B), .Low(mulu_1_low), .Hi(mulu_1_hi));
  Divider #(.width(32)) divider_1 (.out(divider_1_out), .rem(divider_1_rem));  // open: a, b, upper
  Multiplexer #(.select(2), .width(32), .enable("false")) multiplexer_2 (
    .in0(multiplier_1_out), .in1(divu_1_low), .in2(mulu_1_low), .in3(divider_1_out), .out(out_7),
    .sel(SL[1:0]));
  Multiplexer #(.select(2), .width(32), .enable("false")) multiplexer_3 (
    .in0(multiplier_1_cout), .in1(divu_1_hi), .in2(mulu_1_hi), .in3(divider_1_rem), .out(OUT_Hi),
    .sel(SL[1:0]));

  // Other names for the same wires on the sheet: A[31:0] = in_1; CLK = Clock; CRL = Reset; EF = Equality_Flag;
  //   MUL_DiV[1:0] = SL[1:0]; NF = Negative_Flag; Out_Low[31:0] = out_7; OutAlu[31:0] = OutputALU; ZF = Zero_Flag
endmodule

module SLT (
  input  [31:0] RS,
  input  [31:0] RT,
  output [31:0] Output
);

  wire comparator_1_lt;

  Comparator #(.width(32)) comparator_1 (.a(RS), .b(RT), .lt(comparator_1_lt));  // open: gt, eq
  Multiplexer #(.width(32), .enable("false")) multiplexer_1 (
    .in0({32{1'b0}}), .in1(32'h1), .out(Output), .sel(comparator_1_lt));
endmodule

module SLTU (
  input  [31:0] RS,
  input  [31:0] RT,
  output [31:0] Output
);

  wire comparator_1_lt;

  Comparator #(.width(32), .mode("unsigned")) comparator_1 (.a(RS), .b(RT), .lt(comparator_1_lt));  // open: gt, eq
  Multiplexer #(.width(32), .enable("false")) multiplexer_1 (
    .in0({32{1'b0}}), .in1(32'h1), .out(Output), .sel(comparator_1_lt));
endmodule

module MULU (
  input  [31:0] A,
  input  [31:0] B,
  output [31:0] Low,
  output [31:0] Hi
);

  wire C3, Carrier1, Carrier2, CF1, CF2, CF3;
  wire [31:0] A_C2, AL, AR, B_C1, bit_extender_1_out, bit_extender_2_out, bit_extender_3_out,
       bit_extender_4_out, BL, BR, MultHi, MultHi1, MultHi2, MultLow, MultLow1, MultLow2, SumHi1, SumHi2,
       SumLow1, SumLow2;

  Shifter #(.width(32), .shift("lr")) shifter_1 (.in(A), .\dist (5'b00001), .out(AR));
  Shifter #(.width(32), .shift("lr")) shifter_2 (.in(B), .\dist (5'b00001), .out(BR));
  Multiplier #(.width(32)) multiplier_1 (.a(AR), .b(BR), .out(MultLow), .cout(MultHi));  // open: cin
  Shifter #(.width(32)) shifter_3 (.in(AR), .\dist (5'b00001), .out(AL));
  Shifter #(.width(32)) shifter_4 (.in(BR), .\dist (5'b00001), .out(BL));
  Shift_L32 shift_l32_1 (.CIN(1'b0), .in_2(MultLow), .Output(MultLow1), .COutput(Carrier1));
  Shift_L32 shift_l32_2 (.CIN(Carrier1), .in_2(MultHi), .Output(MultHi1));  // open: COutput
  Multiplexer #(.width(32)) multiplexer_1 (.in0({32{1'b0}}), .in1(AL), .out(A_C2), .sel(B[0]));  // open: en
  Multiplexer #(.width(32)) multiplexer_2 (.in0({32{1'b0}}), .in1(BL), .out(B_C1), .sel(A[0]));  // open: en
  and and_1 (C3, A[0], B[0]);
  assign bit_extender_1_out = {{31{1'b0}}, C3};  // Bit_Extender bit_extender_1
  Shift_L32 shift_l32_3 (.CIN(1'b0), .in_2(MultLow1), .Output(MultLow2), .COutput(Carrier2));
  Shift_L32 shift_l32_4 (.CIN(Carrier2), .in_2(MultHi1), .Output(MultHi2));  // open: COutput
  Adder #(.width(32)) adder_1 (.a(MultLow2), .b(A_C2), .out(SumLow1), .cout(CF1));  // open: cin
  Adder #(.width(32)) adder_2 (.a(SumLow1), .b(B_C1), .out(SumLow2), .cout(CF2));  // open: cin
  Adder #(.width(32)) adder_3 (.a(SumLow2), .b(bit_extender_1_out), .out(Low), .cout(CF3));  // open: cin
  // Probe on Low
  // Probe on Hi
  assign bit_extender_2_out = {{31{1'b0}}, CF1};  // Bit_Extender bit_extender_2
  assign bit_extender_3_out = {{31{1'b0}}, CF2};  // Bit_Extender bit_extender_3
  assign bit_extender_4_out = {{31{1'b0}}, CF3};  // Bit_Extender bit_extender_4
  Adder #(.width(32)) adder_4 (.a(MultHi2), .b(bit_extender_2_out), .out(SumHi1));  // open: cin, cout
  Adder #(.width(32)) adder_5 (.a(SumHi1), .b(bit_extender_3_out), .out(SumHi2));  // open: cin, cout
  Adder #(.width(32)) adder_6 (.a(SumHi2), .b(bit_extender_4_out), .out(Hi));  // open: cin, cout

  // Other names for the same wires on the sheet: C1 = A[0]; C2 = B[0]; SumHi[31:0] = Hi; SumLow[31:0] = Low
endmodule

module DIVU (
  input  [31:0] A,
  input  [31:0] B,
  output [31:0] Low,
  output [31:0] Hi
);

  wire xor_1_out;
  wire [31:0] adder_1_out, divider_1_out, mod_1_out_2, mod_2_out_2, xor_2_out;

  MOD mod_1 (.in_1(A), .out_2(mod_1_out_2));
  MOD mod_2 (.in_1(B), .out_2(mod_2_out_2));
  xor xor_1 (xor_1_out, A[31], B[31]);
  Divider #(.width(32)) divider_1 (.a(mod_1_out_2), .b(mod_2_out_2), .out(divider_1_out), .rem(Hi));  // open: upper
  assign xor_2_out = divider_1_out ^ {32{1'b1}};  // XOR_Gate xor_2, 32 bits wide
  Adder #(.width(32)) adder_1 (.a(32'h1), .b(xor_2_out), .out(adder_1_out));  // open: cin, cout
  Multiplexer #(.width(32), .enable("false")) multiplexer_1 (
    .in0(divider_1_out), .in1(adder_1_out), .out(Low), .sel(xor_1_out));
endmodule

module INSTRUCTION_DECODER (
  input  [31:0] Data_In,
  output Nop,
  output TTY,
  output MFLO,
  output SLT,
  output MULU,
  output AND,
  output XOR,
  output BLEZ,
  output J,
  output PUSH,
  output ADDi,
  output ORi,
  output [4:0] Registro_Destino,
  output [15:0] Constante,
  output Halt,
  output KBD,
  output ADD,
  output SLTU,
  output DIV,
  output OR,
  output BEQ,
  output BGTZ,
  output JR,
  output LW,
  output SLTi,
  output XORi,
  output [4:0] RT,
  output [31:0] \Constante_Inmed_No_Lógica ,
  output [25:0] Destino__Jump,
  output RND,
  output MFHI,
  output SUB,
  output MULT,
  output DIVU,
  output NOR,
  output BNEQ,
  output BLTZ,
  output POP,
  output SW,
  output ANDi,
  output SLTiU,
  output [4:0] RS,
  output [31:0] \Constante_Inmed_Lógica 
);

  wire Div_Mul_OP, Funct_Code____0, Funct_Code____1, \Op_Aritmética , OP_Code____000xxx, OP_Code____001xxx,
       OpCode____1, PUSH_POP;

  and and_1 (OpCode____1, Data_In[26], Data_In[27], Data_In[28], Data_In[29], Data_In[30], Data_In[31]);
  and and_2 (\Op_Aritmética , ~Data_In[26], ~Data_In[27], ~Data_In[28], ~Data_In[29], ~Data_In[30], ~Data_In[31]);  // AND_Gate
  and and_3 (Funct_Code____1, Data_In[0], Data_In[1], Data_In[2], Data_In[3], Data_In[4], Data_In[5]);
  and and_4 (Funct_Code____0, ~Data_In[0], ~Data_In[1], ~Data_In[2], ~Data_In[3], ~Data_In[4], ~Data_In[5]);  // AND_Gate
  and and_5 (Halt, OpCode____1, Funct_Code____1);
  and and_6 (Nop, \Op_Aritmética , Funct_Code____0);
  and and_7 (MFHI, \Op_Aritmética , ~Data_In[0], ~Data_In[1], ~Data_In[2], ~Data_In[3], Data_In[4], ~Data_In[5]);  // AND_Gate
  and and_8 (MFLO, \Op_Aritmética , ~Data_In[0], Data_In[1], ~Data_In[2], ~Data_In[3], Data_In[4], ~Data_In[5]);  // AND_Gate
  and and_9 (TTY, OpCode____1, ~Halt, Data_In[0]);  // AND_Gate
  and and_10 (RND, OpCode____1, ~Halt, Data_In[1]);  // AND_Gate
  and and_11 (KBD, OpCode____1, ~Halt, Data_In[2]);  // AND_Gate
  and and_12 (Div_Mul_OP, \Op_Aritmética , Data_In[4], ~Data_In[5]);  // AND_Gate
  and and_13 (ADD, \Op_Aritmética , Data_In[5], ~Data_In[4], ~Data_In[3], ~Data_In[2], ~Data_In[1], ~Data_In[0]);  // AND_Gate
  and and_14 (SUB, \Op_Aritmética , Data_In[5], ~Data_In[4], ~Data_In[3], ~Data_In[2], Data_In[1], ~Data_In[0]);  // AND_Gate
  and and_15 (SLT, \Op_Aritmética , Data_In[5], ~Data_In[4], Data_In[3], ~Data_In[2], Data_In[1], ~Data_In[0]);  // AND_Gate
  and and_16 (SLTU, \Op_Aritmética , Data_In[5], ~Data_In[4], Data_In[3], ~Data_In[2], Data_In[1], Data_In[0]);  // AND_Gate
  and and_17 (MULT, \Op_Aritmética , Div_Mul_OP, Data_In[3], ~Data_In[2], ~Data_In[1], ~Data_In[0]);  // AND_Gate
  and and_18 (DIV, \Op_Aritmética , Div_Mul_OP, Data_In[3], ~Data_In[2], Data_In[1], ~Data_In[0]);  // AND_Gate
  and and_19 (OP_Code____000xxx, ~Data_In[29], ~Data_In[30], ~Data_In[31]);  // AND_Gate
  and and_20 (BEQ, OP_Code____000xxx, Data_In[28], ~Data_In[27], ~Data_In[26]);  // AND_Gate
  and and_21 (BNEQ, OP_Code____000xxx, Data_In[28], ~Data_In[27], Data_In[26]);  // AND_Gate
  and and_22 (BLEZ, OP_Code____000xxx, Data_In[28], Data_In[27], ~Data_In[26]);  // AND_Gate
  and and_23 (BGTZ, OP_Code____000xxx, Data_In[28], Data_In[27], Data_In[26]);
  and and_24 (AND, \Op_Aritmética , Data_In[5], ~Data_In[4], ~Data_In[3], Data_In[2], ~Data_In[1], ~Data_In[0]);  // AND_Gate
  and and_25 (OR, \Op_Aritmética , Data_In[5], ~Data_In[4], ~Data_In[3], Data_In[2], ~Data_In[1], Data_In[0]);  // AND_Gate
  and and_26 (NOR, \Op_Aritmética , Data_In[5], ~Data_In[4], ~Data_In[3], Data_In[2], Data_In[1], Data_In[0]);  // AND_Gate
  and and_27 (XOR, \Op_Aritmética , Data_In[5], ~Data_In[4], Data_In[3], ~Data_In[2], ~Data_In[1], ~Data_In[0]);  // AND_Gate
  and and_28 (MULU, \Op_Aritmética , Div_Mul_OP, Data_In[3], ~Data_In[2], ~Data_In[1], Data_In[0]);  // AND_Gate
  and and_29 (DIVU, \Op_Aritmética , Div_Mul_OP, Data_In[3], ~Data_In[2], Data_In[1], Data_In[0]);  // AND_Gate
  and and_30 (BLTZ, OP_Code____000xxx, ~Data_In[28], ~Data_In[27], Data_In[26]);  // AND_Gate
  and and_31 (J, OP_Code____000xxx, ~Data_In[28], Data_In[27], ~Data_In[26]);  // AND_Gate
  and and_32 (JR, \Op_Aritmética , Data_In[3], ~Data_In[4], ~Data_In[5]);  // AND_Gate
  and and_33 (PUSH_POP, ~Data_In[26], ~Data_In[27], ~Data_In[28], Data_In[29], Data_In[30], Data_In[31]);  // AND_Gate
  and and_34 (PUSH, PUSH_POP, Data_In[0]);
  and and_35 (POP, PUSH_POP, ~Data_In[0]);  // AND_Gate
  and and_36 (LW, Data_In[26], Data_In[27], ~Data_In[28], ~Data_In[29], ~Data_In[30], Data_In[31]);  // AND_Gate
  and and_37 (SW, Data_In[26], Data_In[27], ~Data_In[28], Data_In[29], ~Data_In[30], Data_In[31]);  // AND_Gate
  and and_38 (OP_Code____001xxx, Data_In[29], ~Data_In[30], ~Data_In[31]);  // AND_Gate
  and and_39 (ADDi, OP_Code____001xxx, ~Data_In[28], ~Data_In[27], ~Data_In[26]);  // AND_Gate
  and and_40 (SLTi, OP_Code____001xxx, ~Data_In[28], Data_In[27], ~Data_In[26]);  // AND_Gate
  and and_41 (SLTiU, OP_Code____001xxx, ~Data_In[28], Data_In[27], Data_In[26]);  // AND_Gate
  and and_42 (ANDi, OP_Code____001xxx, Data_In[28], ~Data_In[27], ~Data_In[26]);  // AND_Gate
  and and_43 (ORi, OP_Code____001xxx, Data_In[28], ~Data_In[27], Data_In[26]);  // AND_Gate
  and and_44 (XORi, OP_Code____001xxx, Data_In[28], Data_In[27], ~Data_In[26]);  // AND_Gate

  assign Constante = Data_In[15:0];
  assign \Constante_Inmed_Lógica  = {{16{1'b0}}, Data_In[15:0]};
  assign \Constante_Inmed_No_Lógica  = {{17{Data_In[15]}}, Data_In[14:0]};
  assign Destino__Jump = Data_In[25:0];
  assign Registro_Destino = Data_In[15:11];
  assign RS = Data_In[25:21];
  assign RT = Data_In[20:16];

  // Other names for the same wires on the sheet: Jump_Destiny[25:0] = Data_In[25:0]; Const[15:0] = Data_In[15:0];
  //   F0 = Data_In[0]; Funct_Code[5:0] = Data_In[5:0]; Logical_Inmed_Constante[15:0] = Data_In[15:0];
  //   No_Logical_Inmed_Constante[31:0] = {{17{Data_In[15]}}, Data_In[14:0]}; F1 = Data_In[1]; F2 = Data_In[2];
  //   F3 = Data_In[3]; F4 = Data_In[4]; F5 = Data_In[5]; RD[4:0] = Data_In[15:11]; C0 = Data_In[26];
  //   OpCode[5:0] = Data_In[31:26]; C1 = Data_In[27]; C2 = Data_In[28]; OpCode____0 = \Op_Aritmética 

  // Notes on the sheet:
  //   Outs
  //   Hatl and Nop
  //   porque necesito el halt aqui
  //   si el halt no esta activo es que se activan los demas
  //   MFHI and MFLO
  //   TTY,  RND and  KBD
  //   Aritmetic and Logic
  //   Branch Operation
  //   Push and  Pop
  //   LW and SW
  //   Inmediate Operation
endmodule

module Shift_L32 (
  input  CIN,
  input  [31:0] in_2,
  output [31:0] Output,
  output COutput
);


  assign COutput = in_2[31];
  assign Output = {in_2[30:0], CIN};
endmodule

module MOD (
  input  [31:0] in_1,
  output [31:0] out_2
);

  wire [31:0] negator_1_out;

  Negator #(.width(32)) negator_1 (.in(in_1), .out(negator_1_out));
  Multiplexer #(.width(32), .enable("false")) multiplexer_1 (
    .in0(in_1), .in1(negator_1_out), .out(out_2), .sel(in_1[31]));

  // Other names for the same wires on the sheet: X[31:0] = in_1; XOut[31:0] = out_2
endmodule

module BCU (
  input  NF,
  input  BEQ,
  input  ZF,
  input  EF,
  input  BNE,
  input  BLEZ,
  input  [31:0] PC,
  input  BLTZ,
  input  BGTZ,
  input  [31:0] REGISTER,
  input  J,
  input  JR,
  input  [25:0] Etiqueta_Destino,
  input  [15:0] Offset,
  output [31:0] New_PC
);

  wire and_1_out, and_2_out, and_3_out, and_4_out, and_5_out, and_6_out, GOTO, JMP, or_1_out;
  wire [31:0] adder_1_out, adder_2_out, multiplexer_1_out, multiplexer_2_out;

  or or_1 (or_1_out, NF, ZF);
  and and_1 (and_1_out, ~ZF, ~NF);  // AND_Gate
  and and_2 (and_2_out, BEQ, EF);
  and and_3 (and_3_out, ~EF, BNE);  // AND_Gate
  and and_4 (and_4_out, BLEZ, or_1_out);
  and and_5 (and_5_out, BLTZ, NF);
  and and_6 (and_6_out, BGTZ, and_1_out);
  or or_2 (GOTO, J, JR);
  Adder #(.width(32)) adder_1 (
    .a(adder_2_out), .b({{15{Offset[15]}}, Offset[14:0], 2'b00}), .out(adder_1_out));  // open: cin, cout
  Multiplexer #(.width(32), .enable("false")) multiplexer_1 (
    .in0({PC[31:28], Etiqueta_Destino, 2'b00}), .in1(REGISTER), .out(multiplexer_1_out), .sel(JR));
  Adder #(.width(32)) adder_2 (.a(PC), .b(32'h4), .out(adder_2_out));  // open: cin, cout
  Multiplexer #(.width(32), .enable("false")) multiplexer_2 (
    .in0(adder_1_out), .in1(multiplexer_1_out), .out(multiplexer_2_out), .sel(GOTO));
  or or_3 (JMP, and_2_out, and_3_out, and_4_out, and_5_out, and_6_out, GOTO);
  Multiplexer #(.width(32), .enable("false")) multiplexer_3 (
    .in0(adder_2_out), .in1(multiplexer_2_out), .out(New_PC), .sel(JMP));

  // Other names for the same wires on the sheet: Destino[31:2] = {PC[31:28], Etiqueta_Destino};
  //   ED[25:0] = Etiqueta_Destino; Off[15:0] = Offset; Offset_t[31:2] = {{15{Offset[15]}}, Offset[14:0]}
endmodule

module CU (
  input  Halt,
  input  DIVU,
  input  Nop,
  input  BEQ,
  input  TTY,
  input  BNEQ,
  input  RND,
  input  BLEZ,
  input  KBD,
  input  BGTZ,
  input  MFHI,
  input  BLTZ,
  input  MFLO,
  input  J,
  input  KBD_AV,
  input  ADD,
  input  JR,
  input  SUB,
  input  POP,
  input  SLT,
  input  PUSH,
  input  SLTU,
  input  ADDi,
  input  AND,
  input  SLTi,
  input  OR,
  input  SLTUi,
  input  NOR,
  input  ANDi,
  input  XOR,
  input  ORi,
  input  MULT,
  input  XORi,
  input  DIV,
  input  LW,
  input  MULU,
  input  SW,
  input  EI,
  input  EM,
  output [3:0] Function_Selector,
  output Stack_Inst,
  output Push_Pop,
  output R_W,
  output Lo_Hi_Write,
  output [1:0] ALU_S,
  output [2:0] RF_S,
  output RT_S,
  output R_W_M,
  output L_PC,
  output nR_W,
  output KBD_EN
);

  wire and_1_out, and_2_out, and_3_out, and_7_out, and_8_out, LogicalXi, or_1_out, or_2_out, or_6_out,
       or_8_out, or_9_out, or_10_out, or_13_out, or_14_out, or_15_out, Xi;

  or or_1 (or_1_out, BEQ, BLEZ, BLTZ, BNEQ, BGTZ, J, JR);
  or or_2 (or_2_out, PUSH, SW);
  or or_3 (RT_S, ADDi, SLTi, SLTUi, ANDi, ORi, XORi, LW);
  and and_1 (and_1_out, KBD, ~KBD_AV);  // AND_Gate
  and and_2 (and_2_out, or_1_out, EI);
  and and_3 (and_3_out, EI, ~J, ~BNEQ, ~BGTZ, ~BEQ, ~BLTZ, ~JR, ~BLEZ);  // AND_Gate
  or or_4 (R_W_M, SW, LW, POP, PUSH);
  and and_4 (nR_W, or_2_out, EM);
  or or_5 (L_PC, and_2_out, and_3_out);
  or or_6 (or_6_out, EI, EM);
  Pull_Resistor pull_resistor_1 (.node(RF_S));
  Priority_Encoder #(.disabled(0)) priority_encoder_1 (
    .in1(RND), .in2(POP), .in3(LW), .in4(MFHI), .in5(MFLO), .in6(KBD), .in7(and_1_out), .out(RF_S));  // open: in0, en_in, gs, en_out
  // Probe on RF_S
  or or_7 (Lo_Hi_Write, MULT, MULU, DIV, DIVU);
  or or_8 (or_8_out, LW, SW, ADD, ADDi);
  or or_9 (or_9_out, SLTU, SLTUi);
  or or_10 (or_10_out, OR, ORi);
  or or_11 (LogicalXi, ANDi, ORi, XORi);
  // Probe on Push_Pop
  Priority_Encoder #(.select(1), .disabled(0)) priority_encoder_2 (
    .in0(POP), .in1(PUSH), .out(Push_Pop));  // open: gs, en_out, en_in
  or or_12 (Stack_Inst, POP, PUSH);
  and and_5 (KBD_EN, EI, KBD);
  and and_6 (R_W, ~BEQ, ~Halt, ~BNEQ, ~Nop, ~BLEZ, ~TTY, or_6_out, ~BGTZ, ~SW, ~PUSH, ~J, ~BLTZ, ~JR);  // AND_Gate
  or or_13 (or_13_out, SLT, SLTi);
  or or_14 (or_14_out, AND, ANDi);
  or or_15 (or_15_out, XOR, XORi);
  or or_16 (Xi, LW, SW, ADDi, SLTi, SLTUi, LogicalXi);
  Pull_Resistor pull_resistor_2 (.node(Push_Pop));
  and and_7 (and_7_out, Xi, LogicalXi);
  and and_8 (and_8_out, Xi, ~LogicalXi);  // AND_Gate
  Priority_Encoder #(.select(4), .disabled(0)) priority_encoder_3 (
    .in0(or_8_out), .in1(SUB), .in2(or_13_out), .in3(or_9_out), .in4(or_14_out), .in5(or_10_out), .in6(NOR),
    .in7(or_15_out), .in8(MULT), .in9(DIV), .in10(MULU), .in11(DIVU), .out(Function_Selector));  // open: in12, in13, in14, in15, gs, en_out, en_in
  Priority_Encoder #(.select(2), .disabled(0)) priority_encoder_4 (
    .in1(and_7_out), .in2(and_8_out), .out(ALU_S));  // open: in0, in3, gs, en_out, en_in
  Pull_Resistor pull_resistor_3 (.node(ALU_S));
  // Probe on ALU_S

  // Other names for the same wires on the sheet: ALU_RB_S[1:0] = ALU_S; RF_DATA_IN_S[2:0] = RF_S; SLTiU = SLTUi;
  //   Stack_Ins = Stack_Inst

  // Notes on the sheet:
  //   Memory Control
  //   Program Counter
  //   Register File Control
  //   Stack Control
  //   Case KBD
  //   ALU Control
endmodule

module MC (
  input  Start,
  input  [31:0] RAM_Out_0,
  input  Clock,
  input  Reset,
  input  [31:0] RAM_Out_1,
  input  [3:0] Read_Time,
  input  [3:0] Write_Time,
  input  [31:0] RAM_Out_2,
  input  R_W_Selector,
  input  [31:0] RAM_Out_3,
  input  [31:0] Offset,
  input  [31:0] Registro,
  output Finish,
  output [3:0] Mask,
  output nRead_Write,
  output [31:0] Out,
  output Chip_Select,
  output [15:0] Address,
  output [31:0] RAM_In_0,
  output [31:0] RAM_In_1,
  output [31:0] RAM_In_2,
  output [31:0] RAM_In_3
);

  wire CS0, d_ff_1_q, Dec, demultiplexer_1_out0, Load, Load0, or_1_out, or_4_out, or_5_out, RW_time_ended;
  wire [3:0] Counter_q, multiplexer_1_out;
  wire [31:0] demultiplexer_2_out1;

  Multiplexer #(.width(4), .enable("false")) multiplexer_1 (
    .in0(Read_Time), .in1(Write_Time), .out(multiplexer_1_out), .sel(R_W_Selector));
  or or_1 (or_1_out, demultiplexer_1_out0, Finish);
  Counter #(.width(4), .max('hf)) Counter (
    .load(Load), .D(multiplexer_1_out), .count(Dec), .Q(Counter_q), .clk(Clock));  // open: carry, clr
  or or_2 (Load, Load0, Dec);
  or or_3 (Chip_Select, CS0, Finish);
  D_Flip_Flop d_ff_1 (.clk(Clock), .D(or_1_out), .Q(d_ff_1_q), .preset(or_4_out));  // open: Qn, en, reset
  Demultiplexer #(.enable("false")) demultiplexer_1 (
    .out0(demultiplexer_1_out0), .out1(Load0), .in(d_ff_1_q), .sel(Start));
  or or_4 (or_4_out, ~Start, Reset);  // OR_Gate
  and and_1 (RW_time_ended, ~Counter_q[0], ~Counter_q[1], ~Counter_q[2], ~Counter_q[3]);  // AND_Gate
  Multiplexer #(.select(2), .width(32), .enable("false")) multiplexer_2 (
    .in0(RAM_Out_0), .in1(RAM_Out_1), .in2(RAM_Out_2), .in3(RAM_Out_3),
    .out({Out[7:0], Out[15:8], Out[23:16], Out[31:24]}), .sel(Offset[3:2]));
  Demultiplexer #(.width(32), .enable("false")) demultiplexer_2 (
    .out1(demultiplexer_2_out1), .in({Registro[7:0], Registro[15:8], Registro[23:16], Registro[31:24]}),
    .sel(R_W_Selector));  // open: out0
  D_Flip_Flop While (.clk(Clock), .D(or_5_out), .Q(CS0));  // open: Qn, preset, en, reset
  or or_5 (or_5_out, Dec, Load0);
  Decoder #(.select(2), .enable("false")) decoder_1 (
    .out0(Mask[0]), .out1(Mask[1]), .out2(Mask[2]), .out3(Mask[3]), .sel(Offset[3:2]));
  Demultiplexer #(.select(2), .width(32), .enable("false")) demultiplexer_3 (
    .out0(RAM_In_0), .out1(RAM_In_1), .out2(RAM_In_2), .out3(RAM_In_3), .in(demultiplexer_2_out1),
    .sel(Offset[3:2]));
  Demultiplexer #(.enable("false")) demultiplexer_4 (.out0(Dec), .out1(Finish), .in(CS0), .sel(RW_time_ended));

  assign Address = Offset[19:4];
  assign nRead_Write = R_W_Selector;

  // Other names for the same wires on the sheet: Clk = Clock; CLR = Reset; CS = Chip_Select; End = Finish;
  //   Load1 = Dec; Block[1:0] = Offset[3:2]; ADDR[15:0] = Offset[19:4]; RAM_INPUT_0[31:0] = RAM_In_0;
  //   RAM_INPUT_1[31:0] = RAM_In_1; RAM_INPUT_2[31:0] = RAM_In_2; RAM_INPUT_3[31:0] = RAM_In_3; RAM_MASK[3:0] = Mask;
  //   RAM_OUTPUT_0[31:0] = RAM_Out_0; RAM_OUTPUT_1[31:0] = RAM_Out_1; RAM_OUTPUT_2[31:0] = RAM_Out_2;
  //   RAM_OUTPUT_3[31:0] = RAM_Out_3; RW_Time_Selector = R_W_Selector
endmodule
